# Fritzing sketch schematics (saved by Fritzing 0.9.2b)
circuit board: 9.69795cm x 9.75586cm
breadboards: 2

parts:
  BREAKOUT1 = Adafruit Ultimate GPS Breakout
  BAT1 = BC9VPC [package=bc9vpc]
  M1 = DC Motor
  Arduino_Nano = Arduino Nano (Rev3.0)
  J1 = screw terminal, 2 pins
  U2 = L293D [package=THT]
  BREAKOUT2 = HMC5883L Compass Breakout
  U6 = Voltage Regulator - 5V [package="TO220 [THT]"]
  C2 = Electrolytic Capacitor [capacitance=4.7µF voltage=10V package="100 mil [THT, electrolytic]"]
  C3 = Electrolytic Capacitor [capacitance=0.1mF voltage=20V package="100 mil [THT, electrolytic]"]
  R1 = Resistor [tolerance=±1% resistance=100k package=THT]
  R2 = Resistor [tolerance=±1% resistance=100k package=THT]
  R3 = Resistor [tolerance=±1% resistance=100k package=THT]
  U4 = mystery part, 10 pins [chip_label=ACE]

nets:
  N1: BREAKOUT1.EN, Arduino_Nano.A2
  N2: BREAKOUT1.TX, Arduino_Nano.A1
  N3: BREAKOUT1.RX, Arduino_Nano.A0
  GND: BREAKOUT1.GND, BAT1.V-, Arduino_Nano.GND, U2.0V, BREAKOUT2.GND, U6.GND, C2.-, C3.-, R3.Pin_1, U4.pin8
  VIN: BREAKOUT1.VIN, Arduino_Nano.5V, U2.+Vmotor, U2.+V, BREAKOUT2.VIN, U6.output_voltage, C2.+
  N4: BAT1.V+, U6.input_voltage, C3.+, R1.Pin_0
  N5: M1.pin_1, J1.pin2, U2.Out_1_(_Controlled_by_Enable_1_)
  N6: M1.pin_2, J1.pin1, U2.Out_2_(_Controlled_by_Enable_1_)
  N7: Arduino_Nano.D2, U4.pin1
  N8: Arduino_Nano.D3, U4.pin2
  N9: Arduino_Nano.D4, U4.pin4
  N10: Arduino_Nano.D5, U4.pin5
  N11: Arduino_Nano.D6, U4.pin6
  N12: Arduino_Nano.D7, U4.pin7
  N13: Arduino_Nano.D8, U4.pin9
  N14: Arduino_Nano.D9, U4.pin10
  N15: Arduino_Nano.D10, U2.In_2
  N16: Arduino_Nano.D11/MOSI, U2.In_1
  N17: Arduino_Nano.D12/MISO, U2.Enable_1
  N18: Arduino_Nano.A6, R2.Pin_0, R3.Pin_0
  N19: Arduino_Nano.A5, BREAKOUT2.SCL
  N20: Arduino_Nano.A4, BREAKOUT2.SDA
  N21: R1.Pin_1, R2.Pin_1

notes:
  7.5 V - 15 V
  V+
  V-
