# Fritzing sketch schematics (saved by Fritzing 0.9.2b)
circuit board: 9.69795cm x 9.75586cm
breadboards: 2

parts:
  BREAKOUT1 = Adafruit Ultimate GPS Breakout
  U1 = Voltage Regulator [package=to220-igo]
  C1 = Capacitor Polarized [package=cpol-radial-10uf-25v]
  BAT1 = BC9VPC [package=bc9vpc]
  M1 = DC Motor
  U5 = mystery part, 9 pins [chip_label="RN 4K7"]
  U4 = mystery part, 10 pins [chip_label=ACE]
  Arduino_Nano = Arduino Nano (Rev3.0)
  R1 = Resistor [tolerance=±5% resistance=1 power=2W package=THT]
  R2 = Resistor [tolerance=±5% resistance=1 power=2W package=THT]
  J1 = screw terminal, 2 pins
  U2 = L293D [package=THT]
  BREAKOUT2 = HMC5883L Compass Breakout
  S1 = Pushbutton [package=THT]

nets:
  N1: BREAKOUT1.EN, Arduino_Nano.A2
  N2: BREAKOUT1.TX, Arduino_Nano.A1
  N3: BREAKOUT1.RX, Arduino_Nano.A0
  GND: BREAKOUT1.GND, U1.GND, C1.-, BAT1.V-, U4.pin8, Arduino_Nano.GND, U2.0V, BREAKOUT2.GND, S1.leg1
  VIN: BREAKOUT1.VIN, U1.OUT, C1.+, U5.pin1, Arduino_Nano.5V, U2.+Vmotor, U2.+V, BREAKOUT2.VIN
  N4: U1.IN, BAT1.V+
  N5: M1.pin_1, R1.Pin_1, J1.pin2
  N6: M1.pin_2, R2.Pin_1, J1.pin1
  N7: U5.pin2, U4.pin10, Arduino_Nano.D9
  N8: U5.pin3, U4.pin9, Arduino_Nano.D8
  N9: U5.pin4, U4.pin7, Arduino_Nano.D7
  N10: U5.pin5, U4.pin6, Arduino_Nano.D6
  N11: U5.pin6, U4.pin5, Arduino_Nano.D5
  N12: U5.pin7, U4.pin4, Arduino_Nano.D4
  N13: U5.pin8, U4.pin2, Arduino_Nano.D3
  N14: U5.pin9, U4.pin1, Arduino_Nano.D2
  N15: Arduino_Nano.D10, U2.In_2
  N16: Arduino_Nano.D11/MOSI, U2.In_1
  N17: Arduino_Nano.D12/MISO, U2.Enable_1
  N18: Arduino_Nano.A6, BREAKOUT2.RDY
  N19: Arduino_Nano.A5, BREAKOUT2.SCL
  N20: Arduino_Nano.A4, BREAKOUT2.SDA
  N21: Arduino_Nano.A3, S1.leg0
  N22: R1.Pin_0, U2.Out_1_(_Controlled_by_Enable_1_)
  N23: R2.Pin_0, U2.Out_2_(_Controlled_by_Enable_1_)

notes:
  - Non-standard pinout on 7805!
  - Capacitor graphics has inverse polarity!
  7.5 V - 20 V (25 V?)
  V+
  V-
  it's very probably enough to use internal pullups in Nano
